// Logisim project lista17_cs1.circ as structural Verilog: 1 circuit, main circuit main
module main (
);

  wire and_1_out, and_2_out, clock_1_out, S1, S2, t_ff_1_qn;
  wire [1:0] t_ff_1_q;

  Clock clock_1 (.out(clock_1_out));
  // Probe on t_ff_1_q
  T_Flip_Flop t_ff_1 (.clk(clock_1_out), .T(S1), .Q(t_ff_1_q[0]), .Qn(t_ff_1_qn));  // open: preset, reset, en
  T_Flip_Flop t_ff_2 (.clk(clock_1_out), .T(S2), .Q(t_ff_1_q[1]), .Qn(S1));  // open: preset, reset, en
  and and_1 (and_1_out, t_ff_1_q[1], t_ff_1_q[0]);
  or or_1 (S2, and_1_out, and_2_out);
  and and_2 (and_2_out, S1, t_ff_1_qn);
endmodule
